// Logisim project ALU.circ as structural Verilog: 1 circuit, main circuit main
module main (
);

  wire dipswitch_2_sw2, dipswitch_2_sw3, dipswitch_2_sw4, dipswitch_2_sw5, n7404_1_pin2, n7404_1_pin4,
       n7404_1_pin5, n7404_1_pin6, n7404_1_pin8, n7404_1_pin9, n7404_1_pin10, n7404_1_pin12, n7408_1_pin3,
       n7408_1_pin6, n7408_1_pin8, n7408_1_pin11, n7408_2_pin3, n7408_2_pin6, n7408_2_pin8, n7408_2_pin11,
       n7408_3_pin3, n7408_3_pin6, n7408_3_pin8, n7408_3_pin11, n7432_1_pin11, n7432_2_pin11, n7432_3_pin3,
       n7432_3_pin6, n7432_3_pin8, n7432_3_pin11, n7485_1_pin2, n7485_1_pin3, n7485_1_pin5, n7485_1_pin6,
       n7485_1_pin7, n7486_1_pin1, n7486_1_pin2, n7486_1_pin3, n7486_1_pin5, n7486_1_pin6, n7486_1_pin8,
       n7486_1_pin9, n7486_1_pin11, n7486_1_pin12, n7486_1_pin13, n7486_2_pin1, n7486_2_pin3, n7486_2_pin4,
       n7486_2_pin6, n7486_2_pin10, n7486_2_pin13, n7486_3_pin1, n7486_3_pin3, n7486_3_pin6, n7486_3_pin8,
       n7486_3_pin9, n7486_3_pin11, n7486_3_pin13, n7486_4_pin3, n7486_4_pin6, n7486_4_pin8, n7486_4_pin11,
       n74157_1_pin4, n74157_1_pin7, n74157_1_pin9, n74157_1_pin12, n74157_2_pin3, n74157_2_pin4,
       n74157_2_pin6, n74157_2_pin7, n74157_2_pin9, n74157_2_pin10, n74157_2_pin12, n74157_2_pin13,
       pull_resistor_1_node, pull_resistor_2_node, pull_resistor_3_node, pull_resistor_4_node,
       pull_resistor_5_node;

  _7486 u_7486_1 (
    .pin1(n7486_1_pin1), .pin2(n7486_1_pin2), .pin3(n7486_1_pin3), .pin4(n7486_1_pin3), .pin5(n7486_1_pin5),
    .pin6(n7486_1_pin6), .pin13(n7486_1_pin13), .pin12(n7486_1_pin12), .pin11(n7486_1_pin11),
    .pin10(n7486_1_pin11), .pin9(n7486_1_pin9), .pin8(n7486_1_pin8));
  _7408 u_7408_1 (
    .pin1(n7486_1_pin2), .pin2(n7486_1_pin1), .pin3(n7408_1_pin3), .pin4(n7486_1_pin3), .pin5(n7486_1_pin5),
    .pin6(n7408_1_pin6), .pin13(n7486_1_pin12), .pin12(n7486_1_pin13), .pin11(n7408_1_pin11),
    .pin10(n7486_1_pin11), .pin9(n7486_1_pin9), .pin8(n7408_1_pin8));
  _7486 u_7486_2 (
    .pin1(n7486_2_pin1), .pin2(n7486_1_pin5), .pin3(n7486_2_pin3), .pin4(n7486_2_pin4), .pin5(n7486_1_pin5),
    .pin6(n7486_2_pin6), .pin13(n7486_2_pin13), .pin12(n7486_1_pin5), .pin11(n7486_1_pin2),
    .pin10(n7486_2_pin10), .pin9(n7486_1_pin5), .pin8(n7486_1_pin12));
  _7432 u_7432_1 (
    .pin1(n7408_1_pin6), .pin2(n7408_1_pin3), .pin3(n7486_1_pin9), .pin13(n7408_1_pin11),
    .pin12(n7408_1_pin8), .pin11(n7432_1_pin11));  // open: pin4, pin5, pin6, pin10, pin9, pin8
  _7486 u_7486_3 (
    .pin1(n7486_3_pin1), .pin2(n7486_2_pin3), .pin3(n7486_3_pin3), .pin4(n7486_3_pin3), .pin5(n7432_1_pin11),
    .pin6(n7486_3_pin6), .pin13(n7486_3_pin13), .pin12(n7486_2_pin6), .pin11(n7486_3_pin11),
    .pin10(n7486_3_pin11), .pin9(n7486_3_pin9), .pin8(n7486_3_pin8));
  _7408 u_7408_2 (
    .pin1(n7486_2_pin3), .pin2(n7486_3_pin1), .pin3(n7408_2_pin3), .pin4(n7486_3_pin3), .pin5(n7432_1_pin11),
    .pin6(n7408_2_pin6), .pin13(n7486_2_pin6), .pin12(n7486_3_pin13), .pin11(n7408_2_pin11),
    .pin10(n7486_3_pin11), .pin9(n7486_3_pin9), .pin8(n7408_2_pin8));
  _7432 u_7432_2 (
    .pin1(n7408_2_pin3), .pin2(n7408_2_pin6), .pin3(n7486_3_pin9), .pin13(n7408_2_pin11),
    .pin12(n7408_2_pin8), .pin11(n7432_2_pin11));  // open: pin4, pin5, pin6, pin10, pin9, pin8
  // DipSwitch dipswitch_1: pin names not known; wires that end beside it: n7486_3_pin13, n7486_3_pin1, n7486_1_pin13, n7486_1_pin1, n7486_2_pin4, n7486_2_pin1, n7486_2_pin10, n7486_2_pin13
  DipSwitch dipswitch_2 (
    .sw1(n7486_1_pin5), .sw2(dipswitch_2_sw2), .sw3(dipswitch_2_sw3), .sw4(dipswitch_2_sw4),
    .sw5(dipswitch_2_sw5));  // open: sw6, sw7, sw8
  _7486 u_7486_4 (
    .pin1(n7486_3_pin13), .pin2(n7486_2_pin4), .pin3(n7486_4_pin3), .pin4(n7486_3_pin1), .pin5(n7486_2_pin1),
    .pin6(n7486_4_pin6), .pin13(n7486_1_pin13), .pin12(n7486_2_pin10), .pin11(n7486_4_pin11),
    .pin10(n7486_1_pin1), .pin9(n7486_2_pin13), .pin8(n7486_4_pin8));
  _7485 u_7485_1 (
    .pin1(n7486_3_pin13), .pin2(n7485_1_pin2), .pin3(n7485_1_pin3), .pin4(n7485_1_pin2), .pin5(n7485_1_pin5),
    .pin6(n7485_1_pin6), .pin7(n7485_1_pin7), .pin15(n7486_2_pin4), .pin14(n7486_3_pin1),
    .pin13(n7486_2_pin1), .pin12(n7486_1_pin13), .pin11(n7486_2_pin10), .pin10(n7486_1_pin1),
    .pin9(n7486_2_pin13));
  _7432 u_7432_3 (
    .pin1(n7486_3_pin1), .pin2(n7486_2_pin1), .pin3(n7432_3_pin3), .pin4(n7486_3_pin13), .pin5(n7486_2_pin4),
    .pin6(n7432_3_pin6), .pin13(n7486_2_pin10), .pin12(n7486_1_pin13), .pin11(n7432_3_pin11),
    .pin10(n7486_1_pin1), .pin9(n7486_2_pin13), .pin8(n7432_3_pin8));
  _74157 u_74157_1 (
    .pin1(dipswitch_2_sw2), .pin2(n7485_1_pin7), .pin3(n7486_1_pin6), .pin4(n74157_1_pin4),
    .pin5(n7485_1_pin6), .pin6(n7486_1_pin8), .pin7(n74157_1_pin7), .pin15(n7485_1_pin2),
    .pin14(n7485_1_pin2), .pin13(n7486_3_pin8), .pin12(n74157_1_pin12), .pin11(n7485_1_pin5),
    .pin10(n7486_3_pin6), .pin9(n74157_1_pin9));
  _7408 u_7408_3 (
    .pin1(n7486_3_pin13), .pin2(n7486_2_pin4), .pin3(n7408_3_pin3), .pin4(n7486_3_pin1), .pin5(n7486_2_pin1),
    .pin6(n7408_3_pin6), .pin13(n7486_2_pin10), .pin12(n7486_1_pin13), .pin11(n7408_3_pin11),
    .pin10(n7486_1_pin1), .pin9(n7486_2_pin13), .pin8(n7408_3_pin8));
  _74157 u_74157_2 (
    .pin1(dipswitch_2_sw3), .pin2(n74157_1_pin4), .pin3(n74157_2_pin3), .pin4(n74157_2_pin4),
    .pin5(n74157_1_pin7), .pin6(n74157_2_pin6), .pin7(n74157_2_pin7), .pin15(n7485_1_pin2),
    .pin14(n74157_1_pin12), .pin13(n74157_2_pin13), .pin12(n74157_2_pin12), .pin11(n74157_1_pin9),
    .pin10(n74157_2_pin10), .pin9(n74157_2_pin9));
  _7404 u_7404_1 (
    .pin1(n7486_3_pin13), .pin2(n7404_1_pin2), .pin3(n7486_3_pin1), .pin4(n7404_1_pin4), .pin5(n7404_1_pin5),
    .pin6(n7404_1_pin6), .pin13(n7486_1_pin13), .pin12(n7404_1_pin12), .pin11(n7486_1_pin1),
    .pin10(n7404_1_pin10), .pin9(n7404_1_pin9), .pin8(n7404_1_pin8));
  // NoConnect on n7404_1_pin9
  // NoConnect on n7404_1_pin8
  // NoConnect on n7404_1_pin5
  // NoConnect on n7404_1_pin6
  _74153 u_74153_1 (
    .pin1(n7485_1_pin2), .pin2(dipswitch_2_sw5), .pin3(n7432_3_pin8), .pin4(n7408_3_pin8),
    .pin5(n7486_4_pin8), .pin6(n7404_1_pin10), .pin7(n74157_2_pin3), .pin15(n7485_1_pin2),
    .pin14(dipswitch_2_sw4), .pin13(n7432_3_pin11), .pin12(n7408_3_pin11), .pin11(n7486_4_pin11),
    .pin10(n7404_1_pin12), .pin9(n74157_2_pin6));
  Pull_Resistor pull_resistor_1 (.node(pull_resistor_1_node));
  Pull_Resistor pull_resistor_2 (.node(pull_resistor_2_node));
  LED led_1 (.in(n7432_2_pin11));
  LED led_2 (.in(n74157_2_pin12));
  _74153 u_74153_2 (
    .pin1(n7485_1_pin2), .pin2(dipswitch_2_sw5), .pin3(n7432_3_pin3), .pin4(n7408_3_pin6),
    .pin5(n7486_4_pin6), .pin6(n7404_1_pin4), .pin7(n74157_2_pin10), .pin15(n7485_1_pin2),
    .pin14(dipswitch_2_sw4), .pin13(n7432_3_pin6), .pin12(n7408_3_pin3), .pin11(n7486_4_pin3),
    .pin10(n7404_1_pin2), .pin9(n74157_2_pin13));
  Pull_Resistor pull_resistor_3 (.node(pull_resistor_3_node));
  Pull_Resistor pull_resistor_4 (.node(pull_resistor_4_node));
  LED led_3 (.in(n74157_2_pin9));
  LED led_4 (.in(n74157_2_pin7));
  Pull_Resistor pull_resistor_5 (.node(pull_resistor_5_node));
  LED led_5 (.in(n74157_2_pin4));
  // also tied to GND on the sheet: n7485_1_pin2
  // also tied to VCC on the sheet: n7485_1_pin3
endmodule
